# Fritzing sketch node_garden (saved by Fritzing 0.9.0b)
perfboards: 1

parts:
  Luminosity_Sensor = Color Sensor Breakout ADJD-S311  # not connected
  Moisture_Sensor_3 = female pin header, 4 pins [form="♀ (female)"]
  Moisture_Sensor_4 = female pin header, 4 pins [form="♀ (female)"]
  To_Main_Board1 = male pin header, 6 pins [form="♂ (male)"]
  part = HTU21D Breakout

nets:
  N1: Moisture_Sensor_3.pin1, Moisture_Sensor_4.pin1, To_Main_Board1.pin1, part.3.3V
  N2: Moisture_Sensor_3.pin2, Moisture_Sensor_4.pin2, To_Main_Board1.pin2, part.GND
  N3: Moisture_Sensor_3.pin4, To_Main_Board1.pin4
  N4: Moisture_Sensor_4.pin4, To_Main_Board1.pin3
  N5: To_Main_Board1.pin5, part.SCL
  N6: To_Main_Board1.pin6, part.SDA

custom parts:
  HTU21D Breakout: This is a breadboard friendly breakout board for the Measurement Specialties high-precision, low-power digital humidity sensor.
